# Fritzing sketch ChickenFeeder (saved by Fritzing 0.8.7b)

parts:
  Arduino = Arduino Nano (Rev3.0)
  LCM1602_IIC1 = LCM1602 IIC [part_number="LCM1602 IIC" chip_label="LCM1602 IIC" package="DIP (Dual Inline) [THT]"]
  LCD1 = LCD screen
  Down = Round Pushbutton
  UP = Round Pushbutton
  Set = Round Pushbutton
  Start = Round Pushbutton
  MH-Real-Time_Clock_Module_3 = RTC_DS1302_module
  12V_DC_WATER_PUMP1 = water pump/motor
  Relay_Module = Jtron 1 Channel Optoisolated Relay Module [package=relay]
  DC_Converter = Mini-360 DC-DC Buck converter [package=THT]
  Power_plug1 = Power plug
  ServoMotor = Tower Pro SG90 servo [part_number=101246]

nets:
  GND: Arduino.GND, LCM1602_IIC1.GND, Down.leg1, UP.leg1, Set.leg1, Start.leg1, MH-Real-Time_Clock_Module_3.GND, Relay_Module.GND, DC_Converter.OUT-, ServoMotor.GND
  N1: Arduino.D3, MH-Real-Time_Clock_Module_3.CLK
  N2: Arduino.D4, MH-Real-Time_Clock_Module_3.DAT
  N3: Arduino.D5, MH-Real-Time_Clock_Module_3.RST
  N4: Arduino.D6, Relay_Module.IN1
  N5: Arduino.D7, ServoMotor.Signal
  N6: Arduino.VIN, DC_Converter.OUT+
  VCC: Arduino.5V, LCM1602_IIC1.VCC, MH-Real-Time_Clock_Module_3.VCC, Relay_Module.VCC, ServoMotor.+5V
  N7: Arduino.A5, LCM1602_IIC1.SCL
  N8: Arduino.A4, LCM1602_IIC1.SDA
  N9: Arduino.A3, Down.leg0
  N10: Arduino.A2, UP.leg0
  N11: Arduino.A1, Set.leg0
  N12: Arduino.A0, Start.leg0
  VSS: LCM1602_IIC1.VSS, LCD1.VSS
  VDD: LCM1602_IIC1.VDD, LCD1.VDD
  N13: LCM1602_IIC1.V0, LCD1.V0
  N14: LCM1602_IIC1.RS, LCD1.RS
  N15: LCM1602_IIC1.RW, LCD1.R/W
  N16: LCM1602_IIC1.E, LCD1.E
  N17: LCM1602_IIC1.D0, LCD1.DB0
  N18: LCM1602_IIC1.D1, LCD1.DB1
  N19: LCM1602_IIC1.D2, LCD1.DB2
  N20: LCM1602_IIC1.D3, LCD1.DB3
  N21: LCM1602_IIC1.D4, LCD1.DB4
  N22: LCM1602_IIC1.D5, LCD1.DB5
  N23: LCM1602_IIC1.D6, LCD1.DB6
  N24: LCM1602_IIC1.D7, LCD1.DB7
  N25: LCM1602_IIC1.A, LCD1.LED+
  N26: LCM1602_IIC1.K, LCD1.LED-
  N27: 12V_DC_WATER_PUMP1.pin_1, Relay_Module.MAIN
  N28: 12V_DC_WATER_PUMP1.pin_2, DC_Converter.IN+, Power_plug1.VCC
  N29: Relay_Module.NO, DC_Converter.IN-, Power_plug1.GND

custom parts:
  LCM1602 IIC: I2C-Module to use a 1602 or 2004 LCD on with the wire.h libory Serial LCD Modul
  RTC_DS1302_module: Arduino module DS1302 SPI Real Time Clock
  water pump/motor: WATER PUMP BY ARDUBLOCKTR
  Mini-360 DC-DC Buck converter: Mini-360 DC-DC Buck converter. Tiny buck step down voltage converter, input voltage 4.75 to 23V output 1 to 17V adjustable. Available from ebay and the like.
  Tower Pro SG90 servo: Original file by John De Cristofaro http://www.adafruit.com/products/1449 Adafruit Feedback Servo (Small) Edited by: e-radionica.com 28/9/2015
